# Fritzing sketch testesp1 (saved by Fritzing 0.9.2b)
breadboards: 1

parts:
  YwRobot_Power_Supply1 = YwRobot Breadboard Power Supply [part_number=545043]
  U1 = ESP8266 WiFi Module [part_number=ESP8266]
  Part1 = Arduino Uno (Rev3)
  R1 = Resistor [tolerance=±5% resistance=1k package="0402 [SMD]"]
  LED1 = smd LED [color="Red (633nm)" package="0805 [SMD]"]
  R2 = Resistor [tolerance=±5% resistance=1k package="0402 [SMD]"]
  R3 = Resistor [tolerance=±5% resistance=1k package="0402 [SMD]"]
  R4 = Resistor [tolerance=±5% resistance=1k package="0402 [SMD]"]

nets:
  N1: YwRobot_Power_Supply1.VCC#5, YwRobot_Power_Supply1.VCC#6, U1.VCC, U1.CH_PD
  N2: YwRobot_Power_Supply1.VCC#9, YwRobot_Power_Supply1.VCC#10
  GND: YwRobot_Power_Supply1.GND#11, YwRobot_Power_Supply1.GND#12, U1.GND, Part1.GND, LED1.cathode, R3.Pin_1
  N3: YwRobot_Power_Supply1.GND#13, YwRobot_Power_Supply1.GND#14
  N4: U1.RXD, R1.Pin_1, R2.Pin_0
  N5: U1.TXD, Part1.A2
  N6: Part1.A3, R1.Pin_0
  N7: Part1.A4/SDA, R4.Pin_1
  N8: LED1.anode, R4.Pin_0
  N9: R2.Pin_1, R3.Pin_0

notes:
  change jumper to 3.3v

custom parts:
  YwRobot Breadboard Power Supply: The YwRobot Breadboard Power Supply (MB-V2) has two power rails; they can be 5V or 3V3. Power to the module can be provided through the female USB socket or through the A10 (female) 2.1mm power jack.
  ESP8266 WiFi Module: Generic WiFi Module based on the ESP8266 with onboard PCB antenna and UART communications
